# Fritzing sketch Fritzing (saved by Fritzing 1.0.3b)

parts:
  Part1 = Adafruit ESP32-S3 Feather [part_number="Adafruit #5323"]
  Part3 = Adafruit 1.9in 320x170 TFT [part_number="Adafruit #5394"]
  Part4 = Adafruit MAX98357A I2S 3W Class D Amplifier [part_number="Adafruit #3006"]
  SP1 = SPEAKER [package=pcb_mount_speaker]
  S1 = Round Pushbutton

nets:
  N1: Part1.TX, Part4.LRCLK
  N2: Part1.RX, Part4.BCLK
  N3: Part1.MISO, Part3.MISO
  N4: Part1.MOSI, Part3.MOSI
  N5: Part1.SCK, Part3.SCK
  GND: Part1.GND, Part3.GND, Part4.GND, S1.leg1
  VIN: Part1.3.3V, Part3.VIN, Part4.VIN
  N6: Part1.RESET, Part3.TFTRST
  N7: Part1.D12, S1.leg0
  N8: Part1.D11, Part3.CARDCS
  N9: Part1.D10, Part4.DIN
  N10: Part1.D6, Part3.TFTDC
  N11: Part1.D5, Part3.TFTCS
  N12: Part4.VO-, SP1.+
  N13: Part4.VO+, SP1.-

custom parts:
  Adafruit ESP32-S3 Feather: The ESP32-S3 has arrived in Feather format - and what a great way to get started with this powerful new chip from Espressif! With dual 240 MHz cores, WiFi and BLE support, and native USB, this Feather is great for powering your IoT projects. That's right - it's the new Adafruit ESP32-S3 Feather! With native USB and 8 MB flash, this board will let you upgrade your existing ESP32 projects.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
  Adafruit 1.9in 320x170 TFT: This lovely little display breakout is the best way to add a small, colorful, and very bright display to any project. Since the display uses 4-wire SPI to communicate and has its own pixel-addressable frame buffer, it can be used with every kind of microcontroller. Even a very small one with low memory and few pins available! The 1.9" display has 320x170 16-bit full-color pixels and is an IPS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
  Adafruit MAX98357A I2S 3W Class D Amplifier: Listen to this good news - we now have an all in one digital audio amp breakout board that works incredibly well with the Raspberry Pi! If you're looking for an easy and low cost way to get you digital sound files bumpin' then the MAX08357 I2S Amp Breakout is for you. It takes standard I2S digital audio input and, not only decodes it into analog, but also amplifies it directly into a speaker.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
